// Digital circuit 1x18_RAM.dig as structural Verilog
module _1x18_RAM (
  input  [17:0] WD_17_0,
  input  RS1,
  input  RS2,
  input  WS,
  input  Clk,
  output [17:0] RD1_17_0,
  output [17:0] RD2_17_0
);

  _1x1_RAM _1x1_ram_1 (
    .Write_Data(WD_17_0[5]), .Write_Select(WS), .Read_Select_1(RS1), .Read_Select_2(RS2), .Clk(Clk),
    .Read_Data_1(RD1_17_0[5]), .Read_Data_2(RD2_17_0[5]));
  _1x1_RAM _1x1_ram_2 (
    .Write_Data(WD_17_0[11]), .Write_Select(WS), .Read_Select_1(RS1), .Read_Select_2(RS2), .Clk(Clk),
    .Read_Data_1(RD1_17_0[11]), .Read_Data_2(RD2_17_0[11]));
  _1x1_RAM _1x1_ram_3 (
    .Write_Data(WD_17_0[2]), .Write_Select(WS), .Read_Select_1(RS1), .Read_Select_2(RS2), .Clk(Clk),
    .Read_Data_1(RD1_17_0[2]), .Read_Data_2(RD2_17_0[2]));
  _1x1_RAM _1x1_ram_4 (
    .Write_Data(WD_17_0[17]), .Write_Select(WS), .Read_Select_1(RS1), .Read_Select_2(RS2), .Clk(Clk),
    .Read_Data_1(RD1_17_0[17]), .Read_Data_2(RD2_17_0[17]));
  _1x1_RAM _1x1_ram_5 (
    .Write_Data(WD_17_0[8]), .Write_Select(WS), .Read_Select_1(RS1), .Read_Select_2(RS2), .Clk(Clk),
    .Read_Data_1(RD1_17_0[8]), .Read_Data_2(RD2_17_0[8]));
  _1x1_RAM _1x1_ram_6 (
    .Write_Data(WD_17_0[14]), .Write_Select(WS), .Read_Select_1(RS1), .Read_Select_2(RS2), .Clk(Clk),
    .Read_Data_1(RD1_17_0[14]), .Read_Data_2(RD2_17_0[14]));
  _1x1_RAM _1x1_ram_7 (
    .Write_Data(WD_17_0[16]), .Write_Select(WS), .Read_Select_1(RS1), .Read_Select_2(RS2), .Clk(Clk),
    .Read_Data_1(RD1_17_0[16]), .Read_Data_2(RD2_17_0[16]));
  _1x1_RAM _1x1_ram_8 (
    .Write_Data(WD_17_0[7]), .Write_Select(WS), .Read_Select_1(RS1), .Read_Select_2(RS2), .Clk(Clk),
    .Read_Data_1(RD1_17_0[7]), .Read_Data_2(RD2_17_0[7]));
  _1x1_RAM _1x1_ram_9 (
    .Write_Data(WD_17_0[13]), .Write_Select(WS), .Read_Select_1(RS1), .Read_Select_2(RS2), .Clk(Clk),
    .Read_Data_1(RD1_17_0[13]), .Read_Data_2(RD2_17_0[13]));
  _1x1_RAM _1x1_ram_10 (
    .Write_Data(WD_17_0[4]), .Write_Select(WS), .Read_Select_1(RS1), .Read_Select_2(RS2), .Clk(Clk),
    .Read_Data_1(RD1_17_0[4]), .Read_Data_2(RD2_17_0[4]));
  _1x1_RAM _1x1_ram_11 (
    .Write_Data(WD_17_0[10]), .Write_Select(WS), .Read_Select_1(RS1), .Read_Select_2(RS2), .Clk(Clk),
    .Read_Data_1(RD1_17_0[10]), .Read_Data_2(RD2_17_0[10]));
  _1x1_RAM _1x1_ram_12 (
    .Write_Data(WD_17_0[1]), .Write_Select(WS), .Read_Select_1(RS1), .Read_Select_2(RS2), .Clk(Clk),
    .Read_Data_1(RD1_17_0[1]), .Read_Data_2(RD2_17_0[1]));
  _1x1_RAM _1x1_ram_13 (
    .Write_Data(WD_17_0[15]), .Write_Select(WS), .Read_Select_1(RS1), .Read_Select_2(RS2), .Clk(Clk),
    .Read_Data_1(RD1_17_0[15]), .Read_Data_2(RD2_17_0[15]));
  _1x1_RAM _1x1_ram_14 (
    .Write_Data(WD_17_0[6]), .Write_Select(WS), .Read_Select_1(RS1), .Read_Select_2(RS2), .Clk(Clk),
    .Read_Data_1(RD1_17_0[6]), .Read_Data_2(RD2_17_0[6]));
  _1x1_RAM _1x1_ram_15 (
    .Write_Data(WD_17_0[12]), .Write_Select(WS), .Read_Select_1(RS1), .Read_Select_2(RS2), .Clk(Clk),
    .Read_Data_1(RD1_17_0[12]), .Read_Data_2(RD2_17_0[12]));
  _1x1_RAM _1x1_ram_16 (
    .Write_Data(WD_17_0[3]), .Write_Select(WS), .Read_Select_1(RS1), .Read_Select_2(RS2), .Clk(Clk),
    .Read_Data_1(RD1_17_0[3]), .Read_Data_2(RD2_17_0[3]));
  _1x1_RAM _1x1_ram_17 (
    .Write_Data(WD_17_0[9]), .Write_Select(WS), .Read_Select_1(RS1), .Read_Select_2(RS2), .Clk(Clk),
    .Read_Data_1(RD1_17_0[9]), .Read_Data_2(RD2_17_0[9]));
  _1x1_RAM _1x1_ram_18 (
    .Write_Data(WD_17_0[0]), .Write_Select(WS), .Read_Select_1(RS1), .Read_Select_2(RS2), .Clk(Clk),
    .Read_Data_1(RD1_17_0[0]), .Read_Data_2(RD2_17_0[0]));

  // Other names for the same wires on the sheet: RD1_0 = RD1_17_0[0]; RD1_1 = RD1_17_0[1]; RD1_2 = RD1_17_0[2];
  //   RD1_3 = RD1_17_0[3]; RD1_4 = RD1_17_0[4]; RD1_5 = RD1_17_0[5]; RD1_6 = RD1_17_0[6]; RD1_7 = RD1_17_0[7];
  //   RD1_8 = RD1_17_0[8]; RD1_9 = RD1_17_0[9]; RD1_10 = RD1_17_0[10]; RD1_11 = RD1_17_0[11]; RD1_12 = RD1_17_0[12];
  //   RD1_13 = RD1_17_0[13]; RD1_14 = RD1_17_0[14]; RD1_15 = RD1_17_0[15]; RD1_16 = RD1_17_0[16];
  //   RD1_17 = RD1_17_0[17]; RD2_0 = RD2_17_0[0]; RD2_1 = RD2_17_0[1]; RD2_2 = RD2_17_0[2]; RD2_3 = RD2_17_0[3];
  //   RD2_4 = RD2_17_0[4]; RD2_5 = RD2_17_0[5]; RD2_6 = RD2_17_0[6]; RD2_7 = RD2_17_0[7]; RD2_8 = RD2_17_0[8];
  //   RD2_9 = RD2_17_0[9]; RD2_10 = RD2_17_0[10]; RD2_11 = RD2_17_0[11]; RD2_12 = RD2_17_0[12]; RD2_13 = RD2_17_0[13];
  //   RD2_14 = RD2_17_0[14]; RD2_15 = RD2_17_0[15]; RD2_16 = RD2_17_0[16]; RD2_17 = RD2_17_0[17]; WD0 = WD_17_0[0];
  //   WD1 = WD_17_0[1]; WD2 = WD_17_0[2]; WD3 = WD_17_0[3]; WD4 = WD_17_0[4]; WD5 = WD_17_0[5]; WD6 = WD_17_0[6];
  //   WD7 = WD_17_0[7]; WD8 = WD_17_0[8]; WD9 = WD_17_0[9]; WD10 = WD_17_0[10]; WD11 = WD_17_0[11];
  //   WD12 = WD_17_0[12]; WD13 = WD_17_0[13]; WD14 = WD_17_0[14]; WD15 = WD_17_0[15]; WD16 = WD_17_0[16];
  //   WD17 = WD_17_0[17]
endmodule
