// Digital circuit 1x1_RAM.dig as structural Verilog
module _1x1_RAM (
  input  Write_Data,
  input  Write_Select,
  input  Clk,
  input  Read_Select_1,
  input  Read_Select_2,
  output Read_Data_1,
  output Read_Data_2
);

  wire d_ff_1_q, multiplexer_1_out;

  Multiplexer multiplexer_1 (.sel(Write_Select), .in_0(d_ff_1_q), .in_1(Write_Data), .out(multiplexer_1_out));
  D_FF d_ff_1 (.D(multiplexer_1_out), .C(Clk), .Q(d_ff_1_q));  // open: nQ
  and and_1 (Read_Data_1, Read_Select_1, d_ff_1_q);
  and and_2 (Read_Data_2, Read_Select_2, d_ff_1_q);

  // Other names for the same wires on the sheet: RS1 = Read_Select_1; RS2 = Read_Select_2
endmodule
