// Digital circuit 4bit_Prog_Counter.dig as structural Verilog
module _4bit_Prog_Counter (
  input  Clk,
  input  [3:0] I_3_0,
  output [3:0] O_3_0
);

  _1bitRegister _1bitregister_1 (.Din(I_3_0[0]), .Sel(1'b1), .Clk(Clk), .Dout(O_3_0[0]));
  _1bitRegister _1bitregister_2 (.Din(I_3_0[1]), .Sel(1'b1), .Clk(Clk), .Dout(O_3_0[1]));
  _1bitRegister _1bitregister_3 (.Din(I_3_0[2]), .Sel(1'b1), .Clk(Clk), .Dout(O_3_0[2]));
  _1bitRegister _1bitregister_4 (.Din(I_3_0[3]), .Sel(1'b1), .Clk(Clk), .Dout(O_3_0[3]));

  // Other names for the same wires on the sheet: B0 = O_3_0[0]; B1 = O_3_0[1]; B2 = O_3_0[2]; B3 = O_3_0[3];
  //   A0 = I_3_0[0]; A1 = I_3_0[1]; A2 = I_3_0[2]; A3 = I_3_0[3]
endmodule
