// Digital circuit 6bitAdder.dig as structural Verilog
module _6bitAdder (
  input  [5:0] X_5_0,
  input  [5:0] Y_5_0,
  output [5:0] S_5_0,
  output Cout
);

  wire fa_2_cout, fa_3_cout, fa_4_cout, fa_5_cout, fa_6_cout;

  FA fa_1 (.X(X_5_0[5]), .Y(Y_5_0[5]), .Cin(fa_2_cout), .Cout(Cout), .S(S_5_0[5]));
  FA fa_2 (.X(X_5_0[4]), .Y(Y_5_0[4]), .Cin(fa_3_cout), .Cout(fa_2_cout), .S(S_5_0[4]));
  FA fa_3 (.X(X_5_0[3]), .Y(Y_5_0[3]), .Cin(fa_4_cout), .Cout(fa_3_cout), .S(S_5_0[3]));
  FA fa_4 (.X(X_5_0[2]), .Y(Y_5_0[2]), .Cin(fa_5_cout), .Cout(fa_4_cout), .S(S_5_0[2]));
  FA fa_5 (.X(X_5_0[1]), .Y(Y_5_0[1]), .Cin(fa_6_cout), .Cout(fa_5_cout), .S(S_5_0[1]));
  FA fa_6 (.X(X_5_0[0]), .Y(Y_5_0[0]), .Cin(1'b0), .Cout(fa_6_cout), .S(S_5_0[0]));
endmodule
