// Digital circuit 6bitRegester.dig as structural Verilog
module _6bitRegester (
  input  [5:0] Din_5_0,
  input  Sel,
  input  Clk,
  output [5:0] Dout_5_0
);

  _1bitRegister _1bitregister_1 (.Din(Din_5_0[5]), .Sel(Sel), .Clk(Clk), .Dout(Dout_5_0[5]));
  _1bitRegister _1bitregister_2 (.Din(Din_5_0[4]), .Sel(Sel), .Clk(Clk), .Dout(Dout_5_0[4]));
  _1bitRegister _1bitregister_3 (.Din(Din_5_0[3]), .Sel(Sel), .Clk(Clk), .Dout(Dout_5_0[3]));
  _1bitRegister _1bitregister_4 (.Din(Din_5_0[2]), .Sel(Sel), .Clk(Clk), .Dout(Dout_5_0[2]));
  _1bitRegister _1bitregister_5 (.Din(Din_5_0[1]), .Sel(Sel), .Clk(Clk), .Dout(Dout_5_0[1]));
  _1bitRegister _1bitregister_6 (.Din(Din_5_0[0]), .Sel(Sel), .Clk(Clk), .Dout(Dout_5_0[0]));

  // Other names for the same wires on the sheet: _0 = Din_5_0[0]; _1 = Din_5_0[1]; _2 = Din_5_0[2]; _3 = Din_5_0[3];
  //   _4 = Din_5_0[4]; _5 = Din_5_0[5]
endmodule
