// Digital circuit 6bit_ALU.dig as structural Verilog
module _6bit_ALU (
  input  [5:0] A_5_0,
  input  [5:0] B_5_0,
  input  [1:0] OP_1_0,
  output [5:0] O_5_0
);

  wire [5:0] _6bitadder_1_s_5_0, _6bitand_1_o_5_0, _6bitshl_1_o_5_0;

  _6bitAdder _6bitadder_1 (.X_5_0(A_5_0), .Y_5_0(B_5_0), .S_5_0(_6bitadder_1_s_5_0));  // open: Cout
  _6bitAND _6bitand_1 (.A_5_0(A_5_0), .B_5_0(B_5_0), .O_5_0(_6bitand_1_o_5_0));
  _6bitSHL _6bitshl_1 (.A_5_0(A_5_0), .B_5_0(B_5_0), .O_5_0(_6bitshl_1_o_5_0));
  Multiplexer #(.Selector_Bits(2), .Bits(6)) multiplexer_1 (
    .sel(OP_1_0), .in_0(_6bitadder_1_s_5_0), .in_1(_6bitand_1_o_5_0), .in_2(_6bitshl_1_o_5_0),
    .in_3({6{1'b0}}), .out(O_5_0));
endmodule
