// Digital circuit 9x18_RAM.dig as structural Verilog
module _9x18_RAM (
  input  [3:0] WR_3_0,
  input  [17:0] WRD_17_0,
  input  [3:0] RA1_3_0,
  input  [3:0] RA2_3_0,
  input  Clk,
  input  WE,
  output [17:0] RD1_17_0,
  output [17:0] RD2_17_0
);

  wire R1_0, R1_1, R1_2, R1_3, R1_4, R1_5, R1_6, R1_7, R1_8, R2_0, R2_1, R2_2, R2_3, R2_4, R2_5, R2_6, R2_7,
       R2_8, W0, W1, W2, W3, W4, W5, W6, W7, W8, WS0, WS1, WS2, WS3, WS4, WS5, WS6, WS7, WS8;
  wire [17:0] or_1_out, or_2_out, or_3_out, or_4_out, RD1_0, RD1_1, RD1_2, RD1_3, RD1_4, RD1_5, RD1_6, RD1_7,
       RD1_8, RD2_0, RD2_1, RD2_2, RD2_3, RD2_4, RD2_5, RD2_6, RD2_7, RD2_8;

  Decoder #(.Selector_Bits(4)) decoder_1 (
    .sel(WR_3_0), .out_0(W0), .out_1(W1), .out_2(W2), .out_3(W3), .out_4(W4), .out_5(W5), .out_6(W6),
    .out_7(W7), .out_8(W8));  // open: out_9, out_10, out_11, out_12, out_13, out_14, out_15
  Decoder #(.Selector_Bits(4)) decoder_2 (
    .sel(RA1_3_0), .out_0(R1_0), .out_1(R1_1), .out_2(R1_2), .out_3(R1_3), .out_4(R1_4), .out_5(R1_5),
    .out_6(R1_6), .out_7(R1_7), .out_8(R1_8));  // open: out_9, out_10, out_11, out_12, out_13, out_14, out_15
  Decoder #(.Selector_Bits(4)) decoder_3 (
    .sel(RA2_3_0), .out_0(R2_0), .out_1(R2_1), .out_2(R2_2), .out_3(R2_3), .out_4(R2_4), .out_5(R2_5),
    .out_6(R2_6), .out_7(R2_7), .out_8(R2_8));  // open: out_9, out_10, out_11, out_12, out_13, out_14, out_15
  assign or_1_out = RD1_8 | RD1_7 | RD1_6 | RD1_5 | RD1_4;  // Or or_1, 18 bits wide
  assign or_2_out = RD1_3 | RD1_2 | RD1_1 | RD1_0;  // Or or_2, 18 bits wide
  assign or_3_out = RD2_8 | RD2_7 | RD2_6 | RD2_5 | RD2_4;  // Or or_3, 18 bits wide
  assign or_4_out = RD2_3 | RD2_2 | RD2_1 | RD2_0;  // Or or_4, 18 bits wide
  assign RD1_17_0 = or_1_out | or_2_out;  // Or or_5, 18 bits wide
  assign RD2_17_0 = or_3_out | or_4_out;  // Or or_6, 18 bits wide
  _1x18_RAM _1x18_ram_1 (
    .RS1(R1_8), .RS2(R2_8), .WS(WS8), .WD_17_0(WRD_17_0), .Clk(Clk), .RD1_17_0(RD1_8), .RD2_17_0(RD2_8));
  _1x18_RAM _1x18_ram_2 (
    .RS1(R1_5), .RS2(R2_5), .WS(WS5), .WD_17_0(WRD_17_0), .Clk(Clk), .RD1_17_0(RD1_5), .RD2_17_0(RD2_5));
  _1x18_RAM _1x18_ram_3 (
    .RS1(R1_2), .RS2(R2_2), .WS(WS2), .WD_17_0(WRD_17_0), .Clk(Clk), .RD1_17_0(RD1_2), .RD2_17_0(RD2_2));
  and and_1 (WS0, W0, WE);
  and and_2 (WS1, W1, WE);
  and and_3 (WS2, W2, WE);
  _1x18_RAM _1x18_ram_4 (
    .RS1(R1_7), .RS2(R2_7), .WS(WS7), .WD_17_0(WRD_17_0), .Clk(Clk), .RD1_17_0(RD1_7), .RD2_17_0(RD2_7));
  _1x18_RAM _1x18_ram_5 (
    .RS1(R1_4), .RS2(R2_4), .WS(WS4), .WD_17_0(WRD_17_0), .Clk(Clk), .RD1_17_0(RD1_4), .RD2_17_0(RD2_4));
  _1x18_RAM _1x18_ram_6 (
    .RS1(R1_1), .RS2(R2_1), .WS(WS1), .WD_17_0(WRD_17_0), .Clk(Clk), .RD1_17_0(RD1_1), .RD2_17_0(RD2_1));
  and and_4 (WS3, W3, WE);
  and and_5 (WS4, W4, WE);
  and and_6 (WS5, W5, WE);
  _1x18_RAM _1x18_ram_7 (
    .RS1(R1_6), .RS2(R2_6), .WS(WS6), .WD_17_0(WRD_17_0), .Clk(Clk), .RD1_17_0(RD1_6), .RD2_17_0(RD2_6));
  _1x18_RAM _1x18_ram_8 (
    .RS1(R1_3), .RS2(R2_3), .WS(WS3), .WD_17_0(WRD_17_0), .Clk(Clk), .RD1_17_0(RD1_3), .RD2_17_0(RD2_3));
  _1x18_RAM _1x18_ram_9 (
    .RS1(R1_0), .RS2(R2_0), .WS(WS0), .WD_17_0(WRD_17_0), .Clk(Clk), .RD1_17_0(RD1_0), .RD2_17_0(RD2_0));
  and and_7 (WS6, W6, WE);
  and and_8 (WS7, W7, WE);
  and and_9 (WS8, W8, WE);

  // Other names for the same wires on the sheet: WRD[17:0] = WRD_17_0
endmodule
