// Digital circuit CPU.dig as structural Verilog
module CPU (
  input  [3:0] WR_3_0,
  input  [17:0] WRD_17_0,
  input  WE,
  input  Clk,
  input  CPU_EN,
  input  [3:0] RA2,
  input  ZF,
  output [17:0] RD2,
  output [5:0] RD3_2_0,
  output [5:0] B3_5_0,
  output [5:0] A3_5_0,
  output [2:0] R2_2_0,
  output [2:0] R1_2_0,
  output [2:0] D_2_0,
  output [1:0] out_15,
  output [3:0] out_16
);

  wire CPU_Clk, Imm_sel, Jmp_sel, RegEN;
  wire [3:0] _4bit_pc_adder_1_o_3_0, _4bit_prog_counter_1_o_3_0, multiplexer_1_out, OP_Code;
  wire [5:0] _6bit_reg_set_1_b_5_0;
  wire [7:0] Don_t_Care;

  Multiplexer #(.Bits(4)) multiplexer_1 (
    .sel(Jmp_sel), .in_0(_4bit_pc_adder_1_o_3_0), .in_1({D_2_0, out_16[0]}), .out(multiplexer_1_out));
  _4bit_PC_Adder _4bit_pc_adder_1 (.O_3_0(_4bit_pc_adder_1_o_3_0), .I_3_0(_4bit_prog_counter_1_o_3_0));
  _4bit_Prog_Counter _4bit_prog_counter_1 (
    .I_3_0(multiplexer_1_out), .Clk(CPU_Clk), .O_3_0(_4bit_prog_counter_1_o_3_0));
  _9x18_RAM _9x18_ram_1 (
    .WRD_17_0(WRD_17_0), .WR_3_0(WR_3_0), .WE(WE), .RA1_3_0(_4bit_prog_counter_1_o_3_0), .RA2_3_0(RA2),
    .Clk(Clk), .RD1_17_0({OP_Code, D_2_0, out_16[0], R2_2_0[1:0], Don_t_Care}), .RD2_17_0(RD2));
  and and_1 (CPU_Clk, CPU_EN, Clk);
  _6bit_reg_set _6bit_reg_set_1 (
    .WRD_5_0(RD3_2_0), .WR_2_0(D_2_0), .WE(RegEN), .Clk(CPU_Clk), .RA_2_0(D_2_0),
    .RB_2_0({out_16[0], R2_2_0[1:0]}), .A_5_0(A3_5_0), .B_5_0(_6bit_reg_set_1_b_5_0));
  _6bit_ALU _6bit_alu_1 (.A_5_0(A3_5_0), .B_5_0(B3_5_0), .OP_1_0(out_15), .O_5_0(RD3_2_0));
  ControlUnit controlunit_1 (
    .OpCode_3_0(OP_Code), .ZF(ZF), .Op_1_0(out_15), .RegEN(RegEN), .Imm_Sel(Imm_sel), .Jmp_Sel(Jmp_sel));
  Multiplexer #(.Bits(6)) multiplexer_2 (
    .sel(Imm_sel), .in_0(_6bit_reg_set_1_b_5_0), .in_1({out_16[0], R2_2_0[1:0], Don_t_Care[7:5]}),
    .out(B3_5_0));

  assign out_16[3:1] = D_2_0;
  assign R1_2_0 = D_2_0;
  assign R2_2_0[2] = out_16[0];

  // Other names for the same wires on the sheet: Don_t_Care_imm[4:0] = Don_t_Care[4:0];
  //   R2_imm[5:0] = {out_16[0], R2_2_0[1:0], Don_t_Care[7:5]}; R2[2:0] = {out_16[0], R2_2_0[1:0]};
  //   JMP_ADDR[3:0] = {D_2_0, out_16[0]}; R1[2:0] = D_2_0; OP[1:0] = out_15; WR_RAM[3:0] = WR_3_0;
  //   WRD_RAM[17:0] = WRD_17_0

  // Notes on the sheet:
  //   Register Mode( Type of Op = 00) = 2bit(Type of Mode) + 2bit (Op) + 3bit (Reg 1) + 3bit (Reg 2)  + 8bit(Don't care)
  //   Immediate Mode( Type of Op = 01) = 2bit(Type of Mode) + 2bit (Op) + 3bit (Reg 1) + 6bit (Imm Value) +  5bit(Don't care)
  //   Jump Mode( Type of Op = 10) = 2bit(Type of Mode) + 2bit (Op) + 4bit (Adress) + 10bit(Don't care)
  //   ADD(Op = 00)    AND(Op = 01)    SHL(Op = 10)    JMP (Op = 00)    JE(Op = 01)
  //   ADD R1,3------01 00 001 000011 00000
  //   ADD R2,2------01 00 010 000010 00000
  //   ADD R1,R2----00 00 001 010 00000000
  //   AND R1,0------01 01 001 000000 00000
  //   SHL R2,2------01 10 010 000010 00000
  //   ADD R1,1------01 00 001 000001 00000
  //   JMP 0101------10 00 0101  0000000000
  //   ADD R2,1------01 00 010 000001 00000
  //   SHL R2,1-------01 10 010 000001 00000
  //   JE 0010--------10 01 0001 0000000000
endmodule
