// Digital circuit ControlUnit.dig as structural Verilog
module ControlUnit (
  input  [3:0] OpCode_3_0,
  input  ZF,
  output [1:0] Op_1_0,
  output RegEN,
  output Imm_Sel,
  output Jmp_Sel
);

  wire and_1_out, and_3_out, and_4_out, and_5_out, or_1_out;

  and and_1 (and_1_out, ~OpCode_3_0[2], ~OpCode_3_0[3]);  // And
  and and_2 (Imm_Sel, OpCode_3_0[2], ~OpCode_3_0[3]);  // And
  and and_3 (and_3_out, ~OpCode_3_0[2], OpCode_3_0[3]);  // And
  and and_4 (and_4_out, ~OpCode_3_0[0], ~OpCode_3_0[1]);  // And
  and and_5 (and_5_out, OpCode_3_0[0], ~OpCode_3_0[1], ZF);  // And
  or or_1 (or_1_out, and_4_out, and_5_out);
  or or_2 (RegEN, and_1_out, Imm_Sel);
  and and_6 (Jmp_Sel, and_3_out, or_1_out);

  assign Op_1_0 = OpCode_3_0[1:0];
endmodule
